# Fritzing sketch Diagram (saved by Fritzing 0.9.3b)

parts:
  Part1 = Arduino Uno (Rev3)
  U2 = 74HC595 SMD [package="SO16 [SMD]"]
  Disp1 = LBT2088AH [part_number=LBT2088AH]
  Part2 = Thumb Joystick
  LCM1602_IIC1 = LCM1602 IIC [part_number="LCM1602 IIC" chip_label="LCM1602 IIC" package="DIP (Dual Inline) [THT]"]
  U3 = LCD-16X2 [package=lcd-16x2_nosilk]

nets:
  N1: Part1.A0, Part2.HORZ
  N2: Part1.A1, Part2.VERT
  N3: Part1.A4/SDA, LCM1602_IIC1.SDA
  N4: Part1.A5/SCL, LCM1602_IIC1.SCL
  N5: Part1.D8, Disp1.pin2
  N6: Part1.D9_PWM, Disp1.pin1
  N7: Part1.D11_PWM/MOSI, U2.DS
  N8: Part1.D13/SCK, U2.SH_CP, U2.ST_CP
  GND: Part1.GND, U2.OE, Part2.GND
  N9: Part1.D2, Disp1.pin_8
  N10: Part1.D3_PWM, Disp1.pin_7
  N11: Part1.D4, Disp1.pin_6
  N12: Part1.D5_PWM, Disp1.pin_5
  N13: Part1.D6_PWM, Disp1.pin_4
  N14: Part1.D7, Disp1.pin_3
  5V: Part1.5V, U2.VCC
  N15: U2.Q1, Disp1.pin_15
  N16: U2.Q2, Disp1.pin_14
  N17: U2.Q3, Disp1.pin_13
  N18: U2.Q4, Disp1.pin_12
  N19: U2.Q5, Disp1.pin_11
  N20: U2.Q6, Disp1.pin_10
  N21: U2.Q7, Disp1.pin_9
  N22: U2.Q0, Disp1.pin_16
  VSS: LCM1602_IIC1.VSS, U3.VSS
  VDD: LCM1602_IIC1.VDD, U3.VDD
  N23: LCM1602_IIC1.V0, U3.VO
  N24: LCM1602_IIC1.RS, U3.RS
  N25: LCM1602_IIC1.RW, U3.R_W
  N26: LCM1602_IIC1.E, U3.E
  N27: LCM1602_IIC1.D0, U3.DB0
  N28: LCM1602_IIC1.D1, U3.DB1
  N29: LCM1602_IIC1.D2, U3.DB2
  N30: LCM1602_IIC1.D3, U3.DB3
  N31: LCM1602_IIC1.D4, U3.DB4
  N32: LCM1602_IIC1.D5, U3.DB5
  N33: LCM1602_IIC1.D6, U3.DB6
  N34: LCM1602_IIC1.D7, U3.DB7
  N35: LCM1602_IIC1.A, U3.A
  N36: LCM1602_IIC1.K, U3.K

custom parts:
  LCM1602 IIC: I2C-Module to use a 1602 or 2004 LCD on with the wire.h libory Serial LCD Modul
